# Fritzing sketch BSB-Raspi (saved by Fritzing 0.8.3b)
circuit board: 6cm x 4cm
perfboards: 1

parts:
  RCV = STP16NF06 N-Channel Power MOSFET [part_number=IRLB8748PBF]
  SND = STP16NF06 N-Channel Power MOSFET [part_number=IRLB8748PBF]
  Z6_8V = Zener Diode [part_number=BZX55C6V8 breakdown_voltage=6.8V package="300 mil [THT]"]
  22kΩ = Resistor [tolerance=±5% resistance=22k package=THT]
  D1 = Rectifier Diode [part_number=1N4148 package="300 mil [THT]"]
  330Ω = Resistor [tolerance=±5% resistance=330 package=THT]
  Bus_Active = LED - 5mm [color="Green (555nm)" package="5 mm [THT]"]
  1µF = Ceramic Capacitor [capacitance=1µF package="100 mil [THT, multilayer]"]
  150Ω = Resistor [tolerance=±5% resistance=150 package=THT]
  100kΩ = Resistor [tolerance=±5% resistance=100k package=THT]
  100nF = Ceramic Capacitor [capacitance=100nF package="100 mil [THT, multilayer]"]
  74HC04 = Hex Inverter Schmitt Trigger SN74HC14 [package="DIP (Dual Inline)"]
  160Ω = Resistor [tolerance=±5% resistance=150 package=THT]
  4_7kΩ = Resistor [tolerance=±5% resistance=4.7k package=THT]
  D2 = Rectifier Diode [part_number=1N4148 package="300 mil [THT]"]
  R1 = Resistor [tolerance=±5% resistance=10k package=THT]
  R2 = Resistor [tolerance=±5% resistance=4.7k package=THT]
  SE = male pin header, 3 pins [form="♂ (male)"]
  1_5K = Diode [part_number=1.5KE22CA package=diode-1n4001]
  RaspberryPi = shrouded pin header, 26 pins [form="♂ (shrouded male)"]
  BSB_Bus = screw terminal, 4 pins
  RaspberryPi_2 = Raspberry Pi Model B

nets:
  N1: RCV.gate, Z6_8V.anode, 22kΩ.Pin_0
  VCC: RCV.drain, 100nF.1, 74HC04.VCC, RaspberryPi.pin1, RaspberryPi_2.3V3
  N2: RCV.source, 74HC04.1A, R1.Pin_0, RaspberryPi.pin22, RaspberryPi_2.RXD
  N3: SND.gate, 160Ω.Pin_0, D2.anode
  N4: SND.drain, SE.pin2
  GND: SND.source, 22kΩ.Pin_1, 330Ω.Pin_0, 1µF.0, 100kΩ.Pin_1, 100nF.0, 74HC04.GND, 4_7kΩ.Pin_1, R1.Pin_1, R2.Pin_1, 1_5K.A, RaspberryPi.pin24, BSB_Bus.pin2, BSB_Bus.pin3, RaspberryPi_2.GND
  11.8V: Z6_8V.cathode, SE.pin3, 1_5K.C, BSB_Bus.pin1
  N5: D1.cathode, 150Ω.Pin_1
  N6: D1.anode, 74HC04.1Y
  N7: 330Ω.Pin_1, Bus_Active.cathode
  N8: Bus_Active.anode, 74HC04.3Y
  N9: 1µF.1, 150Ω.Pin_0, 100kΩ.Pin_0, 74HC04.2A
  N10: 74HC04.2Y, 74HC04.3A
  N11: 74HC04.4Y, D2.cathode
  N12: 74HC04.4A, 74HC04.5Y
  N13: 74HC04.5A, R2.Pin_0, RaspberryPi.pin16, RaspberryPi_2.#25
  N14: 74HC04.6Y, 160Ω.Pin_1, 4_7kΩ.Pin_0
  N15: 74HC04.6A, RaspberryPi.pin23, RaspberryPi_2.TXD

custom parts:
  STP16NF06 N-Channel Power MOSFET: STP16NF06 N-channel Power MOSFET
  Raspberry Pi Model B: Raspberry Pi (Model B)
